// Logisim project NEXTPC.circ as structural Verilog
module main (
  input  [29:0] INC_PC,
  input  BEQ,
  input  BNE,
  input  J,
  input  ZERO,
  input  [25:0] Imm26,
  output PCSRC,
  output [29:0] Address
);

  wire and_1_out, and_2_out;
  wire [29:0] adder_1_out, bit_extender_1_out;

  assign bit_extender_1_out = {{14{Imm26[15]}}, Imm26[15:0]};  // Bit_Extender bit_extender_1
  Adder #(.width(30)) adder_1 (.a(INC_PC), .b(bit_extender_1_out), .out(adder_1_out));  // open: cin, cout
  Multiplexer #(.width(30), .enable("false")) multiplexer_1 (
    .in0(adder_1_out), .in1({INC_PC[29:26], Imm26}), .out(Address), .sel(J));
  and and_1 (and_1_out, ~ZERO, BNE);  // AND_Gate
  or or_1 (PCSRC, and_1_out, J, and_2_out);
  and and_2 (and_2_out, ZERO, BEQ);
endmodule
