// Logisim project impl.circ as structural Verilog
module adder1 (
  input  A,
  input  B,
  input  CI,
  output R,
  output CO
);

  wire and_1_out, and_2_out, and_3_out, and_4_out, and_5_out, and_6_out, and_7_out, not_1_out, not_2_out,
       not_3_out, not_4_out, not_5_out, not_6_out;

  not not_1 (not_1_out, A);
  not not_2 (not_2_out, B);
  not not_3 (not_3_out, A);
  not not_4 (not_4_out, CI);
  not not_5 (not_5_out, B);
  not not_6 (not_6_out, CI);
  and and_1 (and_1_out, not_1_out, not_2_out, CI);
  and and_2 (and_2_out, not_3_out, B, not_4_out);
  and and_3 (and_3_out, A, not_5_out, not_6_out);
  and and_4 (and_4_out, A, B, CI);
  and and_5 (and_5_out, B, CI);
  or or_1 (CO, and_5_out, and_6_out, and_7_out);
  and and_6 (and_6_out, A, CI);
  and and_7 (and_7_out, A, B);
  or or_2 (R, and_1_out, and_2_out, and_3_out, and_4_out);
endmodule

module adder4 (
  input  [3:0] A,
  input  [3:0] B,
  input  CI,
  output [3:0] R,
  output CO
);

  wire adder1_2_co, adder1_3_co, adder1_4_co;

  adder1 adder1_1 (.A(A[3]), .B(B[3]), .CI(adder1_2_co), .R(R[3]), .CO(CO));
  adder1 adder1_2 (.A(A[2]), .B(B[2]), .CI(adder1_3_co), .R(R[2]), .CO(adder1_2_co));
  adder1 adder1_3 (.A(A[1]), .B(B[1]), .CI(adder1_4_co), .R(R[1]), .CO(adder1_3_co));
  adder1 adder1_4 (.A(A[0]), .B(B[0]), .CI(CI), .R(R[0]), .CO(adder1_4_co));
endmodule

module adder32 (
  input  CI,
  input  [31:0] A,
  input  [31:0] B,
  output [31:0] R,
  output CO
);

  wire adder4_1_co, adder4_2_co, adder4_3_co, adder4_4_co, adder4_5_co, adder4_6_co, adder4_7_co;

  adder4 adder4_1 (.CO(adder4_1_co), .R(R[3:0]), .CI(CI), .B(B[3:0]), .A(A[3:0]));
  adder4 adder4_2 (.CO(adder4_2_co), .R(R[7:4]), .CI(adder4_1_co), .B(B[7:4]), .A(A[7:4]));
  adder4 adder4_3 (.CO(adder4_3_co), .R(R[11:8]), .CI(adder4_2_co), .B(B[11:8]), .A(A[11:8]));
  adder4 adder4_4 (.CO(adder4_4_co), .R(R[15:12]), .CI(adder4_3_co), .B(B[15:12]), .A(A[15:12]));
  adder4 adder4_5 (.CO(adder4_5_co), .R(R[19:16]), .CI(adder4_4_co), .B(B[19:16]), .A(A[19:16]));
  adder4 adder4_6 (.CO(adder4_6_co), .R(R[23:20]), .CI(adder4_5_co), .B(B[23:20]), .A(A[23:20]));
  adder4 adder4_7 (.CO(adder4_7_co), .R(R[27:24]), .CI(adder4_6_co), .B(A[27:24]), .A(B[27:24]));
  adder4 adder4_8 (.CO(CO), .R(R[31:28]), .CI(adder4_7_co), .B(B[31:28]), .A(A[31:28]));
endmodule

module ALUAdder (
  input  AOrS,
  input  [31:0] A,
  input  [31:0] B,
  output [31:0] C,
  output C0
);

  wire [31:0] xor_1_out;

  assign xor_1_out = {32{AOrS}} ^ B;  // XOR_Gate xor_1, 32 bits wide
  adder32 adder32_1 (.CO(C0), .R(C), .B(xor_1_out), .A(A), .CI(AOrS));
endmodule

module LogicUnit (
  input  [31:0] A,
  input  [31:0] B,
  input  [1:0] S,
  output [31:0] O
);

  wire [31:0] and_1_out, not_1_out, or_1_out, xor_1_out;

  assign and_1_out = A & B;  // AND_Gate and_1, 32 bits wide
  assign or_1_out = A | B;  // OR_Gate or_1, 32 bits wide
  assign xor_1_out = A ^ B;  // XOR_Gate xor_1, 32 bits wide
  assign not_1_out = ~or_1_out;  // NOT_Gate not_1, 32 bits wide
  Multiplexer #(.select(2), .width(32), .enable("false")) multiplexer_1 (
    .in0(and_1_out), .in1(or_1_out), .in2(not_1_out), .in3(xor_1_out), .out(O), .sel(S));
endmodule

module ALU (
  input  [31:0] A,
  input  [31:0] B,
  input  [2:0] ALUOp,
  output [31:0] out_4
);

  wire or_1_out;
  wire [31:0] aluadder_1_c, logicunit_1_o;

  ALUAdder aluadder_1 (.AOrS(ALUOp[0]), .A(A), .B(B), .C(aluadder_1_c));  // open: C0
  LogicUnit logicunit_1 (.A(A), .B(B), .S(ALUOp[2:1]), .O(logicunit_1_o));
  or or_1 (or_1_out, ALUOp[1], ALUOp[2]);
  Multiplexer #(.width(32), .enable("false")) multiplexer_1 (
    .in0(aluadder_1_c), .in1(logicunit_1_o), .out(out_4), .sel(or_1_out));
endmodule

module CPU (
  input  C
);

  wire and_1_out, and_2_out, or_1_out, registerfile_1_p3, registerfile_1_p7;
  wire [3:0] mips_alu_1_p3;
  wire [4:0] mipsprogramrom_1_p1_2, multiplexer_3_out, registerfile_1_p5;
  wire [5:0] multiplexer_5_out;
  wire [19:0] mips_alu_1_p5;
  wire [20:0] mipsprogramrom_1_p1;
  wire [29:0] incrementer_1_p4;
  wire [31:0] bit_extender_1_out, mips_ram_1_p6, multiplexer_1_out, multiplexer_2_out, multiplexer_4_out,
       PC_q, registerfile_1_p8;
  wire [31:20] mips_alu_1_p5_2;
  wire [31:26] mipsprogramrom_1_p1_3;

  Register #(.width(32), .trigger("falling")) PC (.D(multiplexer_1_out), .en(1'b1), .clk(C), .Q(PC_q));  // open: clr
  Multiplexer #(.width(32), .enable("false")) multiplexer_1 (
    .in0({incrementer_1_p4, 2'b00}), .in1({32{1'b0}}), .out(multiplexer_1_out), .sel(1'b0));
  and and_1 (and_1_out, mipsprogramrom_1_p1_3[31], ~mipsprogramrom_1_p1_3[30], ~mipsprogramrom_1_p1_3[29], ~mipsprogramrom_1_p1_3[28], mipsprogramrom_1_p1_3[27], mipsprogramrom_1_p1_3[26]);  // AND_Gate
  // Incrementer #(.width(30)) incrementer_1: pin names not known; wires that end beside it: multiplexer_1_out, PC_q[31:2], PC_q, incrementer_1_p4
  Multiplexer #(.width(32), .enable("false")) multiplexer_2 (
    .in0({mips_alu_1_p5_2, mips_alu_1_p5}), .in1(mips_ram_1_p6), .out(multiplexer_2_out), .sel(and_1_out));
  Multiplexer #(.width(5), .enable("false")) multiplexer_3 (
    .in0(mipsprogramrom_1_p1_2), .in1(mipsprogramrom_1_p1[20:16]), .out(multiplexer_3_out), .sel(or_1_out));
  // RegisterFile #(.trigger("falling")) registerfile_1: pin names not known; wires that end beside it: multiplexer_2_out, C, registerfile_1_p3, multiplexer_3_out, registerfile_1_p5, mipsprogramrom_1_p1[20:16], registerfile_1_p7, registerfile_1_p8
  // MIPSProgramROM mipsprogramrom_1: pin names not known; wires that end beside it: {mipsprogramrom_1_p1_3, registerfile_1_p5, mipsprogramrom_1_p1[20:16], mipsprogramrom_1_p1_2, mipsprogramrom_1_p1[10:0]}
  assign bit_extender_1_out = {{16{mipsprogramrom_1_p1_2[4]}}, {mipsprogramrom_1_p1_2, mipsprogramrom_1_p1[10:0]}};  // Bit_Extender bit_extender_1
  not not_1 (registerfile_1_p3, and_2_out);
  Multiplexer #(.width(32), .enable("false")) multiplexer_4 (
    .in0(registerfile_1_p8), .in1(bit_extender_1_out), .out(multiplexer_4_out), .sel(or_1_out));
  and and_2 (and_2_out, mipsprogramrom_1_p1_3[26], mipsprogramrom_1_p1_3[27], ~mipsprogramrom_1_p1_3[28], mipsprogramrom_1_p1_3[29], ~mipsprogramrom_1_p1_3[30], mipsprogramrom_1_p1_3[31]);  // AND_Gate
  or or_1 (or_1_out, mipsprogramrom_1_p1_3[26], mipsprogramrom_1_p1_3[27], mipsprogramrom_1_p1_3[28], mipsprogramrom_1_p1_3[29], mipsprogramrom_1_p1_3[30], mipsprogramrom_1_p1_3[31]);
  // Mips_ALU mips_alu_1: pin names not known; wires that end beside it: registerfile_1_p7, multiplexer_4_out, mips_alu_1_p3, mipsprogramrom_1_p1[10:6], {mips_alu_1_p5_2, mips_alu_1_p5}
  Multiplexer #(.width(6), .enable("false")) multiplexer_5 (
    .in0(mipsprogramrom_1_p1[5:0]), .in1(mipsprogramrom_1_p1_3), .out(multiplexer_5_out), .sel(or_1_out));
  ALUCtrl aluctrl_1 (.I(multiplexer_5_out), .O(mips_alu_1_p3));
  // MIPS_RAM mips_ram_1: pin names not known; wires that end beside it: mips_alu_1_p5, registerfile_1_p8, and_2_out, C, and_1_out, mips_ram_1_p6

  // Notes on the sheet:
  //   contents of mipsprogramrom_1 (hex, n*v repeats v):
  //   addiu $t1, $0, 0xA or $t2, $t0, $t1 sll $t3, $t2, 3 sw $t3, 0($0) lw $t4, 0($0)
endmodule

module WEFunct (
  input  R,
  input  S,
  output WE
);

  not not_1 (WE, S);
endmodule

module ALUCtrl (
  input  [5:0] I,
  output [3:0] O
);

  or or_1 (O[1], I[0], I[3]);

  assign {I[4], I[1]} = {2{I[5]}};
  assign {O[3:2], O[0]} = {I[2], 2'b00};
  // also tied to GND on the sheet: I[5]
endmodule
